// Logisim project furkan_gundogan.circ as structural Verilog: 2 circuits, main circuit main
module main (
  input  in_1,
  input  CLR,
  input  in_3,
  output [15:0] out_4,
  output [2:0] Write_Reg_bit,
  output [15:0] out_6,
  output [15:0] out_7,
  output [15:0] out_8,
  output [2:0] out_9,
  output [2:0] out_10,
  output [2:0] out_11,
  output [15:0] out_12,
  output [15:0] out_13,
  output out_14,
  output [15:0] out_15
);

  wire CLOCK_2_out, CLOCK_3_out, CLOCK_out, demultiplexer_1_out0, demultiplexer_1_out1, demultiplexer_1_out2,
       demultiplexer_1_out3, demultiplexer_1_out4, demultiplexer_1_out5, demultiplexer_1_out6,
       demultiplexer_1_out7;
  wire [15:0] adder_1_out, bit_extender_1_out, multiplexer_2_out, register_2_q, register_3_q, register_4_q,
       register_5_q, register_6_q, register_7_q, register_8_q, register_9_q;

  Clock CLOCK (.out(CLOCK_out));
  Register #(.width(16)) register_1 (.D(adder_1_out), .en(1'b1), .Q(out_6), .clk(CLOCK_out), .clr(in_1));
  Clock CLOCK_2 (.out(CLOCK_2_out));
  Adder #(.width(16)) adder_1 (.a(16'h1), .b(out_6), .out(adder_1_out));  // open: cin, cout
  Multiplexer #(.width(3)) multiplexer_1 (
    .in0(out_7[2:0]), .in1(out_7[8:6]), .out(Write_Reg_bit), .sel(out_14));  // open: en
  RAM #(.addrWidth(16), .dataWidth(16)) ram_1 (
    .addr(out_15), .data(out_12), .sel(1'b1), .clk(CLOCK_2_out), .ld(out_14), .clr(in_3));
  ROM #(.addrWidth(16), .dataWidth(16)) rom_1 (.addr(out_6), .data(out_7), .sel(1'b1));
  and and_1 (out_14, out_7[10], out_7[9]);
  Multiplexer #(.width(16)) multiplexer_2 (
    .in0(out_13), .in1(out_12), .out(multiplexer_2_out), .sel(out_14));  // open: en
  ALU alu_1 (.First_Value(out_4), .Second_Value(out_8), .Fonk(out_7[9]), .out_4(out_13));
  Demultiplexer #(.select(3)) demultiplexer_1 (
    .out0(demultiplexer_1_out0), .out1(demultiplexer_1_out1), .out2(demultiplexer_1_out2),
    .out3(demultiplexer_1_out3), .out4(demultiplexer_1_out4), .out5(demultiplexer_1_out5),
    .out6(demultiplexer_1_out6), .out7(demultiplexer_1_out7), .in(1'b1), .sel(Write_Reg_bit));  // open: en
  Clock CLOCK_3 (.out(CLOCK_3_out));
  assign bit_extender_1_out = {{13{1'b0}}, out_7[2:0]};  // Bit_Extender bit_extender_1
  Register #(.width(16)) register_2 (
    .D(multiplexer_2_out), .en(demultiplexer_1_out0), .Q(register_2_q), .clk(CLOCK_3_out), .clr(CLR));
  Register #(.width(16)) register_3 (
    .D(multiplexer_2_out), .en(demultiplexer_1_out1), .Q(register_3_q), .clk(CLOCK_3_out), .clr(CLR));
  Register #(.width(16)) register_4 (
    .D(multiplexer_2_out), .en(demultiplexer_1_out2), .Q(register_4_q), .clk(CLOCK_3_out), .clr(CLR));
  Register #(.width(16)) register_5 (
    .D(multiplexer_2_out), .en(demultiplexer_1_out3), .Q(register_5_q), .clk(CLOCK_3_out), .clr(CLR));
  Register #(.width(16)) register_6 (
    .D(multiplexer_2_out), .en(demultiplexer_1_out4), .Q(register_6_q), .clk(CLOCK_3_out), .clr(CLR));
  Register #(.width(16)) register_7 (
    .en(demultiplexer_1_out5), .Q(register_7_q), .clk(CLOCK_3_out), .clr(CLR));  // open: D
  Register #(.width(16)) register_8 (
    .D(multiplexer_2_out), .en(demultiplexer_1_out6), .Q(register_8_q), .clk(CLOCK_3_out), .clr(CLR));
  Register #(.width(16)) register_9 (
    .D(multiplexer_2_out), .en(demultiplexer_1_out7), .Q(register_9_q), .clk(CLOCK_3_out), .clr(CLR));
  Adder #(.width(16)) adder_2 (.a(out_8), .b(bit_extender_1_out), .out(out_15));  // open: cin, cout
  Multiplexer #(.select(3), .width(16)) multiplexer_3 (
    .in0(register_2_q), .in1(register_3_q), .in2(register_4_q), .in3(register_5_q), .in4(register_6_q),
    .in5(register_7_q), .in6(register_8_q), .in7(register_9_q), .out(out_4), .sel(out_7[8:6]));  // open: en
  Multiplexer #(.select(3), .width(16)) multiplexer_4 (
    .in0(register_2_q), .in1(register_3_q), .in2(register_4_q), .in3(register_5_q), .in4(register_6_q),
    .in5(register_7_q), .in6(register_8_q), .in7(register_9_q), .out(out_8), .sel(out_7[5:3]));  // open: en

  assign out_9 = out_7[2:0];
  assign out_10 = out_7[5:3];
  assign out_11 = out_7[8:6];

  // Notes on the sheet:
  //   PROGRAM COUNTER
  //   Loaded Data
  //   INSTRUCTION MEMORY
  //   Write Reg bit
  //   contents of rom_1 (hex, n*v repeats v):
  //   0 f 254 79a
  //   Oppcode Controller
  //   ALU result
  //   Alu/LDR
  //   Write Register
  //   ADD/AND
  //   ALU
  //   Ofset value
  //   REGISTER FILE
  //   Address to load
  //   Read Register 1
  //   Read Register 2
endmodule

module ALU (
  input  [15:0] First_Value,
  input  [15:0] Second_Value,
  input  Fonk,
  output [15:0] out_4
);

  wire [15:0] adder_1_out, and_1_out;

  Adder #(.width(16)) adder_1 (.a(First_Value), .b(Second_Value), .out(adder_1_out));  // open: cin, cout
  assign and_1_out = Second_Value & First_Value;  // AND_Gate and_1, 16 bits wide
  Multiplexer #(.width(16)) multiplexer_1 (.in0(adder_1_out), .in1(and_1_out), .out(out_4), .sel(Fonk));  // open: en
endmodule
